// Logisim project 5-bit_multiplier.circ as structural Verilog: 11 circuits, main circuit main
// +
module main (
  input  [4:0] in_1,
  input  [4:0] in_2
);

  wire a1_t, a2_t, a3_t, a4_t, a5, a6, a7, a8, a9, b1_t, b2_t, b3_t, b4_t, b5, b6, b7, b8, b9, c1, c2, c3,
       c4, c5, c6, c7, c8, c9, compl2, CP2, d1, d2, d3, d4, d5, d6, d7, d8, d9,
       decodificador_5_bits_p_display_1_out_3, decodificador_5_bits_p_display_1_out_4,
       decodificador_5_bits_p_display_1_out_5, decodificador_5_bits_p_display_1_out_6,
       decodificador_5_bits_p_display_1_out_7, decodificador_5_bits_p_display_1_out_8,
       decodificador_5_bits_p_display_1_out_9, decodificador_5_bits_p_display_1_out_10,
       decodificador_5_bits_p_display_1_out_11, decodificador_5_bits_p_display_1_out_12,
       decodificador_5_bits_p_display_1_out_13, decodificador_5_bits_p_display_1_out_14,
       decodificador_5_bits_p_display_2_out_3, decodificador_5_bits_p_display_2_out_4,
       decodificador_5_bits_p_display_2_out_5, decodificador_5_bits_p_display_2_out_6,
       decodificador_5_bits_p_display_2_out_7, decodificador_5_bits_p_display_2_out_8,
       decodificador_5_bits_p_display_2_out_9, decodificador_5_bits_p_display_2_out_10,
       decodificador_5_bits_p_display_2_out_11, decodificador_5_bits_p_display_2_out_12,
       decodificador_5_bits_p_display_2_out_13, decodificador_5_bits_p_display_2_out_14,
       decodificador_10_bits_p_display_1_out_3, decodificador_10_bits_p_display_1_out_4,
       decodificador_10_bits_p_display_1_out_5, decodificador_10_bits_p_display_1_out_6,
       decodificador_10_bits_p_display_1_out_7, decodificador_10_bits_p_display_1_out_8,
       decodificador_10_bits_p_display_1_out_9, decodificador_10_bits_p_display_1_out_10,
       decodificador_10_bits_p_display_1_out_11, decodificador_10_bits_p_display_1_out_12,
       decodificador_10_bits_p_display_1_out_13, decodificador_10_bits_p_display_1_out_14, e1, e2, e3, e4,
       e5, e6, e7, e8, e9, f1, f2, f3, f4, f5, f6, f7, f8, f9, g1, g2, g3, g4, g5, g6, g7, g8, g9, n0, n1,
       n2, n7_segment_display_7_p1, n7_segment_display_7_p2;
  wire [4:0] mostrar_5_bits_1_saida_com_sinal, mostrar_5_bits_1_saida_sem_sinal,
       mostrar_5_bits_2_saida_com_sinal, mostrar_5_bits_2_saida_sem_sinal;
  wire [9:0] mostrar_10_bits_1_saida_com_sinal, mostrar_10_bits_1_saida_sem_sinal, P;

  Button Compl__2 (.out(CP2));
  _7_Segment_Display u_7_segment_display_1 (.g(n2));  // open: f, a, b, e, d, c, dp
  BCD_7_Segmentos bcd_7_segmentos_1 (
    .B3(decodificador_5_bits_p_display_1_out_3), .B2(decodificador_5_bits_p_display_1_out_4),
    .B1(decodificador_5_bits_p_display_1_out_5), .B0(decodificador_5_bits_p_display_1_out_6), .a(a3_t),
    .b(b3_t), .c(c3), .d(d3), .e(e3), .f(f3), .g(g3));
  LED led_1 (.in(compl2));
  _7_Segment_Display u_7_segment_display_2 (.g(g2), .f(f2), .a(a2_t), .b(b2_t), .e(e2), .d(d2), .c(c2));  // open: dp
  // Probe on mostrar_5_bits_1_saida_sem_sinal
  Mostrar_5_bits mostrar_5_bits_1 (
    .Entrada(in_1), .Sinal(compl2), .Saida_sem_sinal(mostrar_5_bits_1_saida_sem_sinal),
    .Saida_com_sinal(mostrar_5_bits_1_saida_com_sinal));
  // Probe on mostrar_5_bits_1_saida_com_sinal
  _7_Segment_Display u_7_segment_display_3 (.g(g1), .f(f1), .a(a1_t), .b(b1_t), .e(e1), .d(d1), .c(c1));  // open: dp
  BCD_7_Segmentos bcd_7_segmentos_2 (
    .B3(decodificador_5_bits_p_display_1_out_7), .B2(decodificador_5_bits_p_display_1_out_8),
    .B1(decodificador_5_bits_p_display_1_out_9), .B0(decodificador_5_bits_p_display_1_out_10), .a(a2_t),
    .b(b2_t), .c(c2), .d(d2), .e(e2), .f(f2), .g(g2));
  BCD_7_Segmentos bcd_7_segmentos_3 (
    .B3(decodificador_10_bits_p_display_1_out_3), .B2(decodificador_10_bits_p_display_1_out_4),
    .B1(decodificador_10_bits_p_display_1_out_5), .B0(decodificador_10_bits_p_display_1_out_6), .a(a6),
    .b(b6), .c(c6), .d(d6), .e(e6), .f(f6), .g(g6));
  Decodificador_5_bits_p__display decodificador_5_bits_p_display_1 (
    .Entrada(in_1), .Complemento_de_2(compl2), .out_15(n2), .out_3(decodificador_5_bits_p_display_1_out_3),
    .out_4(decodificador_5_bits_p_display_1_out_4), .out_5(decodificador_5_bits_p_display_1_out_5),
    .out_6(decodificador_5_bits_p_display_1_out_6), .out_7(decodificador_5_bits_p_display_1_out_7),
    .out_8(decodificador_5_bits_p_display_1_out_8), .out_9(decodificador_5_bits_p_display_1_out_9),
    .out_10(decodificador_5_bits_p_display_1_out_10), .out_11(decodificador_5_bits_p_display_1_out_11),
    .out_12(decodificador_5_bits_p_display_1_out_12), .out_13(decodificador_5_bits_p_display_1_out_13),
    .out_14(decodificador_5_bits_p_display_1_out_14));
  // Probe on mostrar_5_bits_2_saida_sem_sinal
  Mostrar_5_bits mostrar_5_bits_2 (
    .Entrada(in_2), .Sinal(compl2), .Saida_sem_sinal(mostrar_5_bits_2_saida_sem_sinal),
    .Saida_com_sinal(mostrar_5_bits_2_saida_com_sinal));
  // Probe on mostrar_5_bits_2_saida_com_sinal
  _7_Segment_Display u_7_segment_display_4 (.g(g8), .f(f8), .a(a8), .b(b8), .e(e8), .d(d8), .c(c8));  // open: dp
  _7_Segment_Display u_7_segment_display_5 (.g(n1));  // open: f, a, b, e, d, c, dp
  BCD_7_Segmentos bcd_7_segmentos_4 (
    .B3(decodificador_5_bits_p_display_1_out_11), .B2(decodificador_5_bits_p_display_1_out_12),
    .B1(decodificador_5_bits_p_display_1_out_13), .B0(decodificador_5_bits_p_display_1_out_14), .a(a1_t),
    .b(b1_t), .c(c1), .d(d1), .e(e1), .f(f1), .g(g1));
  BCD_7_Segmentos bcd_7_segmentos_5 (
    .B3(decodificador_10_bits_p_display_1_out_7), .B2(decodificador_10_bits_p_display_1_out_8),
    .B1(decodificador_10_bits_p_display_1_out_9), .B0(decodificador_10_bits_p_display_1_out_10), .a(a5),
    .b(b5), .c(c5), .d(d5), .e(e5), .f(f5), .g(g5));
  _7_Segment_Display u_7_segment_display_6 (.g(g7), .f(f7), .a(a7), .b(b7), .e(e7), .d(d7), .c(c7));  // open: dp
  Decodificador_10_bits_p__display decodificador_10_bits_p_display_1 (
    .Entrada(P), .Complemento_de_2(compl2), .out_15(n0), .out_3(decodificador_10_bits_p_display_1_out_3),
    .out_4(decodificador_10_bits_p_display_1_out_4), .out_5(decodificador_10_bits_p_display_1_out_5),
    .out_6(decodificador_10_bits_p_display_1_out_6), .out_7(decodificador_10_bits_p_display_1_out_7),
    .out_8(decodificador_10_bits_p_display_1_out_8), .out_9(decodificador_10_bits_p_display_1_out_9),
    .out_10(decodificador_10_bits_p_display_1_out_10), .out_11(decodificador_10_bits_p_display_1_out_11),
    .out_12(decodificador_10_bits_p_display_1_out_12), .out_13(decodificador_10_bits_p_display_1_out_13),
    .out_14(decodificador_10_bits_p_display_1_out_14));
  BCD_7_Segmentos bcd_7_segmentos_6 (
    .B3(decodificador_5_bits_p_display_2_out_3), .B2(decodificador_5_bits_p_display_2_out_4),
    .B1(decodificador_5_bits_p_display_2_out_5), .B0(decodificador_5_bits_p_display_2_out_6), .a(a9), .b(b9),
    .c(c9), .d(d9), .e(e9), .f(f9), .g(g9));
  BCD_7_Segmentos bcd_7_segmentos_7 (
    .B3(decodificador_10_bits_p_display_1_out_11), .B2(decodificador_10_bits_p_display_1_out_12),
    .B1(decodificador_10_bits_p_display_1_out_13), .B0(decodificador_10_bits_p_display_1_out_14), .a(a4_t),
    .b(b4_t), .c(c4), .d(d4), .e(e4), .f(f4), .g(g4));
  // _7_Segment_Display 7_segment_display_7: pin names not known; wires that end beside it: n7_segment_display_7_p1, n7_segment_display_7_p2, n0
  _7_Segment_Display u_7_segment_display_8 (.g(g6), .f(f6), .a(a6), .b(b6), .e(e6), .d(d6), .c(c6));  // open: dp
  BCD_7_Segmentos bcd_7_segmentos_8 (
    .B3(decodificador_5_bits_p_display_2_out_7), .B2(decodificador_5_bits_p_display_2_out_8),
    .B1(decodificador_5_bits_p_display_2_out_9), .B0(decodificador_5_bits_p_display_2_out_10), .a(a8),
    .b(b8), .c(c8), .d(d8), .e(e8), .f(f8), .g(g8));
  Multiplicador multiplicador_1 (.A(in_1), .B(in_2), .Complemento_de_2(CP2), .Sinal(compl2), .Saida(P));
  _7_Segment_Display u_7_segment_display_9 (.g(g5), .f(f5), .a(a5), .b(b5), .e(e5), .d(d5), .c(c5));  // open: dp
  Decodificador_5_bits_p__display decodificador_5_bits_p_display_2 (
    .Entrada(in_2), .Complemento_de_2(compl2), .out_15(n1), .out_3(decodificador_5_bits_p_display_2_out_3),
    .out_4(decodificador_5_bits_p_display_2_out_4), .out_5(decodificador_5_bits_p_display_2_out_5),
    .out_6(decodificador_5_bits_p_display_2_out_6), .out_7(decodificador_5_bits_p_display_2_out_7),
    .out_8(decodificador_5_bits_p_display_2_out_8), .out_9(decodificador_5_bits_p_display_2_out_9),
    .out_10(decodificador_5_bits_p_display_2_out_10), .out_11(decodificador_5_bits_p_display_2_out_11),
    .out_12(decodificador_5_bits_p_display_2_out_12), .out_13(decodificador_5_bits_p_display_2_out_13),
    .out_14(decodificador_5_bits_p_display_2_out_14));
  // Probe on mostrar_10_bits_1_saida_sem_sinal
  Mostrar_10_bits mostrar_10_bits_1 (
    .Entrada(P), .Sinal(compl2), .Saida_sem_sinal(mostrar_10_bits_1_saida_sem_sinal),
    .Saida_com_sinal(mostrar_10_bits_1_saida_com_sinal));
  // Probe on mostrar_10_bits_1_saida_com_sinal
  _7_Segment_Display u_7_segment_display_10 (.g(g4), .f(f4), .a(a4_t), .b(b4_t), .e(e4), .d(d4), .c(c4));  // open: dp
  BCD_7_Segmentos bcd_7_segmentos_9 (
    .B3(decodificador_5_bits_p_display_2_out_11), .B2(decodificador_5_bits_p_display_2_out_12),
    .B1(decodificador_5_bits_p_display_2_out_13), .B0(decodificador_5_bits_p_display_2_out_14), .a(a7),
    .b(b7), .c(c7), .d(d7), .e(e7), .f(f7), .g(g7));

  // Other names for the same wires on the sheet: B[4:0] = in_1; B0 = in_1[0]; B1 = in_1[1]; B2 = in_1[2];
  //   B3 = in_1[3]; B4 = in_1[4]; A[4:0] = in_2; A0 = in_2[0]; A1 = in_2[1]; A2 = in_2[2]; A3 = in_2[3]; A4 = in_2[4];
  //   L = compl2

  // Notes on the sheet:
  //   Aluno 1:
  //   Aluno 2:
  //   Aluno 3:
  //   ________________________________________________________________________________________________________________________________________________
  //   B
  //   Dezena
  //   Claiton Denardi Paulus
  //   OPERANDO B
  //   Unidade
  //   P
  //   Marcelo Oliveira Prates Jr.
  //   Wederson Machado Fagundes
  //   X
  //   OPERANDO A
  //   Dezena
  //   Unidade
  //   Trabalho Escolhido:
  //   Multiplicador Array 5 bits + displays 7 segmentos
  //   A
  //   INTERMEDIARIO
  //   Centena
  //   Dezena
  //   Unidade
  //   01/2018
endmodule

// +
module Somador (
  input  C_in,
  input  A,
  input  B,
  output Saida,
  output C_out
);

  wire and_1_out, and_2_out, xor_2_out;

  or or_1 (C_out, and_1_out, and_2_out);
  xor xor_1 (Saida, C_in, xor_2_out);
  and and_1 (and_1_out, C_in, xor_2_out);
  xor xor_2 (xor_2_out, A, B);
  and and_2 (and_2_out, A, B);

  // Notes on the sheet:
  //   SOMADOR COMPLETO
endmodule

// +/-
module Somado_Subtrator (
  input  A,
  input  B,
  input  C_in,
  input  Mode,
  output Saida,
  output C_out
);

  wire and_1_out, and_2_out, or_2_out, xor_2_out, xor_3_out;

  xor xor_1 (Saida, xor_2_out, C_in);
  or or_1 (C_out, and_2_out, and_1_out);
  and and_1 (and_1_out, xor_3_out, or_2_out);
  xor xor_2 (xor_2_out, A, B);
  and and_2 (and_2_out, C_in, B);
  xor xor_3 (xor_3_out, A, Mode);
  or or_2 (or_2_out, B, C_in);

  // Notes on the sheet:
  //   Somador e Subtrator
endmodule

// x
module Multiplicador_s__sinal (
  input  [4:0] A,
  input  [4:0] B,
  output [9:0] Saida
);

  wire and_1_out, and_2_out, and_3_out, and_4_out, and_5_out, and_6_out, and_7_out, and_8_out, and_9_out,
       and_10_out, and_11_out, and_12_out, and_13_out, and_14_out, and_15_out, and_16_out, and_17_out,
       and_18_out, and_19_out, and_20_out, and_21_out, and_22_out, and_23_out, and_24_out, somador_1_c_out,
       somador_1_saida, somador_2_c_out, somador_2_saida, somador_3_c_out, somador_3_saida, somador_5_c_out,
       somador_5_saida, somador_6_c_out, somador_6_saida, somador_7_c_out, somador_7_saida, somador_8_c_out,
       somador_9_c_out, somador_9_saida, somador_10_c_out, somador_10_saida, somador_11_c_out,
       somador_11_saida, somador_12_c_out, somador_13_c_out, somador_13_saida, somador_14_c_out,
       somador_14_saida, somador_15_c_out, somador_15_saida, somador_16_c_out, somador_17_c_out,
       somador_18_c_out, somador_19_c_out, somador_20_c_out;

  and and_1 (and_1_out, A[1], B[4]);
  Somador somador_1 (.Saida(somador_1_saida), .C_out(somador_1_c_out), .C_in(1'b0), .A(and_1_out), .B(somador_5_c_out));
  and and_2 (and_2_out, A[2], B[4]);
  Somador somador_2 (
    .Saida(somador_2_saida), .C_out(somador_2_c_out), .C_in(somador_6_c_out), .A(and_2_out),
    .B(somador_1_c_out));
  and and_3 (and_3_out, A[3], B[4]);
  Somador somador_3 (
    .Saida(somador_3_saida), .C_out(somador_3_c_out), .C_in(somador_7_c_out), .A(and_3_out),
    .B(somador_2_c_out));
  and and_4 (and_4_out, A[4], B[4]);
  Somador somador_4 (.Saida(Saida[8]), .C_out(Saida[9]), .C_in(somador_8_c_out), .A(and_4_out), .B(somador_3_c_out));
  and and_5 (and_5_out, A[0], B[4]);
  and and_6 (and_6_out, A[1], B[3]);
  Somador somador_5 (
    .Saida(somador_5_saida), .C_out(somador_5_c_out), .C_in(somador_9_c_out), .A(and_6_out), .B(and_5_out));
  and and_7 (and_7_out, A[2], B[3]);
  Somador somador_6 (
    .Saida(somador_6_saida), .C_out(somador_6_c_out), .C_in(somador_10_c_out), .A(and_7_out),
    .B(somador_1_saida));
  and and_8 (and_8_out, A[3], B[3]);
  Somador somador_7 (
    .Saida(somador_7_saida), .C_out(somador_7_c_out), .C_in(somador_11_c_out), .A(and_8_out),
    .B(somador_2_saida));
  and and_9 (and_9_out, A[4], B[3]);
  Somador somador_8 (
    .Saida(Saida[7]), .C_out(somador_8_c_out), .C_in(somador_12_c_out), .A(and_9_out), .B(somador_3_saida));
  and and_10 (and_10_out, A[1], B[2]);
  Somador somador_9 (
    .Saida(somador_9_saida), .C_out(somador_9_c_out), .C_in(somador_13_c_out), .A(and_10_out), .B(and_14_out));
  and and_11 (and_11_out, A[2], B[2]);
  Somador somador_10 (
    .Saida(somador_10_saida), .C_out(somador_10_c_out), .C_in(somador_14_c_out), .A(and_11_out),
    .B(somador_5_saida));
  and and_12 (and_12_out, A[3], B[2]);
  Somador somador_11 (
    .Saida(somador_11_saida), .C_out(somador_11_c_out), .C_in(somador_15_c_out), .A(and_12_out),
    .B(somador_6_saida));
  and and_13 (and_13_out, A[4], B[2]);
  Somador somador_12 (
    .Saida(Saida[6]), .C_out(somador_12_c_out), .C_in(somador_16_c_out), .A(and_13_out), .B(somador_7_saida));
  and and_14 (and_14_out, A[0], B[3]);
  and and_15 (and_15_out, A[1], B[1]);
  and and_16 (and_16_out, A[2], B[1]);
  and and_17 (and_17_out, A[3], B[1]);
  and and_18 (and_18_out, A[4], B[1]);
  and and_19 (and_19_out, A[0], B[2]);
  Somador somador_13 (
    .Saida(somador_13_saida), .C_out(somador_13_c_out), .C_in(somador_17_c_out), .A(and_15_out),
    .B(and_19_out));
  Somador somador_14 (
    .Saida(somador_14_saida), .C_out(somador_14_c_out), .C_in(somador_18_c_out), .A(and_16_out),
    .B(somador_9_saida));
  Somador somador_15 (
    .Saida(somador_15_saida), .C_out(somador_15_c_out), .C_in(somador_19_c_out), .A(and_17_out),
    .B(somador_10_saida));
  Somador somador_16 (
    .Saida(Saida[5]), .C_out(somador_16_c_out), .C_in(somador_20_c_out), .A(and_18_out), .B(somador_11_saida));
  and and_20 (and_20_out, A[0], B[1]);
  and and_21 (and_21_out, A[1], B[0]);
  Somador somador_17 (.Saida(Saida[1]), .C_out(somador_17_c_out), .C_in(1'b0), .A(and_21_out), .B(and_20_out));
  and and_22 (and_22_out, A[2], B[0]);
  Somador somador_18 (.Saida(Saida[2]), .C_out(somador_18_c_out), .C_in(1'b0), .A(and_22_out), .B(somador_13_saida));
  and and_23 (and_23_out, A[3], B[0]);
  Somador somador_19 (.Saida(Saida[3]), .C_out(somador_19_c_out), .C_in(1'b0), .A(and_23_out), .B(somador_14_saida));
  and and_24 (and_24_out, A[4], B[0]);
  Somador somador_20 (.Saida(Saida[4]), .C_out(somador_20_c_out), .C_in(1'b0), .A(and_24_out), .B(somador_15_saida));
  and and_25 (Saida[0], A[0], B[0]);

  // Other names for the same wires on the sheet: P0 = Saida[0]; P1 = Saida[1]; P2 = Saida[2]; P3 = Saida[3];
  //   P4 = Saida[4]; P5 = Saida[5]; P6 = Saida[6]; P7 = Saida[7]; P8 = Saida[8]; P9 = Saida[9]

  // Notes on the sheet:
  //   MULTIPLICADOR 5 BITS SEM SINAL
endmodule

// (-)x
module Multiplicador_c__sinal (
  input  [4:0] A,
  input  [4:0] B,
  output [9:0] Saida
);

  wire and_1_out, and_2_out, and_3_out, and_4_out, and_5_out, and_6_out, and_7_out, and_8_out, and_9_out,
       and_10_out, and_11_out, and_12_out, and_13_out, and_14_out, and_15_out, and_16_out, and_17_out,
       and_18_out, and_19_out, and_20_out, and_21_out, and_22_out, and_23_out, and_24_out,
       somado_subtrator_2_c_out, somado_subtrator_3_c_out, somado_subtrator_4_c_out,
       somado_subtrator_5_c_out, somado_subtrator_6_c_out, somador_1_saida, somador_2_saida, somador_3_saida,
       somador_4_c_out, somador_4_saida, somador_5_c_out, somador_5_saida, somador_6_c_out, somador_6_saida,
       somador_7_c_out, somador_7_saida, somador_8_c_out, somador_8_saida, somador_9_c_out, somador_9_saida,
       somador_10_c_out, somador_10_saida, somador_11_c_out, somador_11_saida, somador_12_c_out,
       somador_12_saida, somador_13_c_out, somador_13_saida, somador_14_c_out, somador_14_saida,
       somador_15_c_out, somador_15_saida, somador_16_c_out, somador_17_c_out, somador_18_c_out;

  Somador somador_1 (.Saida(somador_1_saida), .C_in(somador_4_c_out), .A(and_1_out), .B(and_5_out));  // open: C_out
  Somador somador_2 (
    .Saida(somador_2_saida), .C_in(somador_5_c_out), .A(somador_1_saida), .B(and_2_out));  // open: C_out
  Somador somador_3 (
    .Saida(somador_3_saida), .C_in(somador_6_c_out), .A(somador_2_saida), .B(and_3_out));  // open: C_out
  Somado_Subtrator somado_subtrator_1 (
    .Saida(Saida[9]), .C_in(somado_subtrator_2_c_out), .Mode(somado_subtrator_2_c_out), .A(somador_3_saida),
    .B(and_4_out));  // open: C_out
  and and_1 (and_1_out, A[1], B[4]);
  Somador somador_4 (.Saida(somador_4_saida), .C_out(somador_4_c_out), .C_in(1'b0), .A(and_1_out), .B(somador_7_c_out));
  and and_2 (and_2_out, A[2], B[4]);
  Somador somador_5 (
    .Saida(somador_5_saida), .C_out(somador_5_c_out), .C_in(somador_8_c_out), .A(and_2_out),
    .B(somador_1_saida));
  and and_3 (and_3_out, A[3], B[4]);
  Somador somador_6 (
    .Saida(somador_6_saida), .C_out(somador_6_c_out), .C_in(somador_9_c_out), .A(and_3_out),
    .B(somador_2_saida));
  and and_4 (and_4_out, B[4], A[4]);
  Somado_Subtrator somado_subtrator_2 (
    .Saida(Saida[8]), .C_out(somado_subtrator_2_c_out), .C_in(somado_subtrator_3_c_out), .Mode(A[4]),
    .A(and_4_out), .B(somador_3_saida));
  and and_5 (and_5_out, A[0], B[4]);
  and and_6 (and_6_out, A[1], B[3]);
  Somador somador_7 (
    .Saida(somador_7_saida), .C_out(somador_7_c_out), .C_in(somador_10_c_out), .A(and_6_out), .B(and_5_out));
  and and_7 (and_7_out, A[2], B[3]);
  Somador somador_8 (
    .Saida(somador_8_saida), .C_out(somador_8_c_out), .C_in(somador_11_c_out), .A(and_7_out),
    .B(somador_4_saida));
  and and_8 (and_8_out, A[3], B[3]);
  Somador somador_9 (
    .Saida(somador_9_saida), .C_out(somador_9_c_out), .C_in(somador_12_c_out), .A(and_8_out),
    .B(somador_5_saida));
  and and_9 (and_9_out, B[3], A[4]);
  Somado_Subtrator somado_subtrator_3 (
    .Saida(Saida[7]), .C_out(somado_subtrator_3_c_out), .C_in(somado_subtrator_4_c_out), .Mode(A[4]),
    .A(and_9_out), .B(somador_6_saida));
  and and_10 (and_10_out, A[1], B[2]);
  Somador somador_10 (
    .Saida(somador_10_saida), .C_out(somador_10_c_out), .C_in(somador_13_c_out), .A(and_10_out),
    .B(and_14_out));
  and and_11 (and_11_out, A[2], B[2]);
  Somador somador_11 (
    .Saida(somador_11_saida), .C_out(somador_11_c_out), .C_in(somador_14_c_out), .A(and_11_out),
    .B(somador_7_saida));
  and and_12 (and_12_out, A[3], B[2]);
  Somador somador_12 (
    .Saida(somador_12_saida), .C_out(somador_12_c_out), .C_in(somador_15_c_out), .A(and_12_out),
    .B(somador_8_saida));
  and and_13 (and_13_out, B[2], A[4]);
  and and_14 (and_14_out, A[0], B[3]);
  and and_15 (and_15_out, A[1], B[1]);
  and and_16 (and_16_out, A[2], B[1]);
  and and_17 (and_17_out, A[3], B[1]);
  and and_18 (and_18_out, B[1], A[4]);
  Somado_Subtrator somado_subtrator_4 (
    .Saida(Saida[6]), .C_out(somado_subtrator_4_c_out), .C_in(somado_subtrator_5_c_out), .Mode(A[4]),
    .A(and_13_out), .B(somador_9_saida));
  and and_19 (and_19_out, A[0], B[2]);
  Somador somador_13 (
    .Saida(somador_13_saida), .C_out(somador_13_c_out), .C_in(somador_16_c_out), .A(and_15_out),
    .B(and_19_out));
  Somador somador_14 (
    .Saida(somador_14_saida), .C_out(somador_14_c_out), .C_in(somador_17_c_out), .A(and_16_out),
    .B(somador_10_saida));
  Somador somador_15 (
    .Saida(somador_15_saida), .C_out(somador_15_c_out), .C_in(somador_18_c_out), .A(and_17_out),
    .B(somador_11_saida));
  Somado_Subtrator somado_subtrator_5 (
    .Saida(Saida[5]), .C_out(somado_subtrator_5_c_out), .C_in(somado_subtrator_6_c_out), .Mode(A[4]),
    .A(and_18_out), .B(somador_12_saida));
  and and_20 (and_20_out, A[1], B[0]);
  and and_21 (and_21_out, A[0], B[1]);
  Somador somador_16 (.Saida(Saida[1]), .C_out(somador_16_c_out), .C_in(1'b0), .A(and_20_out), .B(and_21_out));
  and and_22 (and_22_out, A[2], B[0]);
  Somador somador_17 (.Saida(Saida[2]), .C_out(somador_17_c_out), .C_in(1'b0), .A(and_22_out), .B(somador_13_saida));
  and and_23 (and_23_out, A[3], B[0]);
  Somador somador_18 (.Saida(Saida[3]), .C_out(somador_18_c_out), .C_in(1'b0), .A(and_23_out), .B(somador_14_saida));
  and and_24 (and_24_out, B[0], A[4]);
  Somado_Subtrator somado_subtrator_6 (
    .Saida(Saida[4]), .C_out(somado_subtrator_6_c_out), .C_in(1'b0), .Mode(A[4]), .A(and_24_out),
    .B(somador_15_saida));
  and and_25 (Saida[0], A[0], B[0]);

  // Other names for the same wires on the sheet: P0 = Saida[0]; P1 = Saida[1]; P2 = Saida[2]; P3 = Saida[3];
  //   P4 = Saida[4]; P5 = Saida[5]; P6 = Saida[6]; P7 = Saida[7]; P8 = Saida[8]; P9 = Saida[9]

  // Notes on the sheet:
  //   MULTIPLICADOR 5 BITS COM SINAL
endmodule

// M5x5
module Multiplicador (
  input  [4:0] A,
  input  [4:0] B,
  input  Complemento_de_2,
  output [9:0] Saida,
  output Sinal
);

  wire \Mantem_a_operação_em_complemento_de_2_ou_não_qn ;
  wire [9:0] multiplicador_c_sinal_1_saida, multiplicador_s_sinal_1_saida;

  D_Flip_Flop \Mantem_a_operação_em_complemento_de_2_ou_não  (
    .clk(Complemento_de_2), .D(\Mantem_a_operação_em_complemento_de_2_ou_não_qn ), .Q(Sinal),
    .Qn(\Mantem_a_operação_em_complemento_de_2_ou_não_qn ));  // open: preset, en, reset
  Multiplicador_s__sinal multiplicador_s_sinal_1 (.A(A), .B(B), .Saida(multiplicador_s_sinal_1_saida));
  Multiplexer #(.width(10), .enable("false")) multiplexer_1 (
    .in0(multiplicador_s_sinal_1_saida), .in1(multiplicador_c_sinal_1_saida), .out(Saida), .sel(Sinal));
  Multiplicador_c__sinal multiplicador_c_sinal_1 (.A(A), .B(B), .Saida(multiplicador_c_sinal_1_saida));

  // Notes on the sheet:
  //   Escolhe qual das duas operações vai pra saída
endmodule

// BCD-7Seg
module BCD_7_Segmentos (
  input  B3,
  input  B2,
  input  B1,
  input  B0,
  output a,
  output b,
  output c,
  output d,
  output e,
  output f,
  output g
);

  wire and_1_out, and_2_out, and_3_out, and_4_out, and_5_out, and_6_out, and_7_out, and_8_out, and_9_out,
       and_10_out, and_11_out, and_12_out, and_13_out, and_14_out, and_15_out, and_16_out, not_1_out,
       not_2_out, not_3_out, not_4_out, not_5_out, not_6_out, not_7_out, not_8_out, not_9_out, not_10_out,
       not_11_out, not_12_out, not_13_out, not_14_out, not_15_out, not_16_out, not_17_out, not_18_out,
       not_19_out, not_20_out, not_21_out;

  not not_1 (not_1_out, B2);
  and and_1 (and_1_out, not_1_out, not_2_out);
  not not_2 (not_2_out, B0);
  and and_2 (and_2_out, B2, B0);
  not not_3 (not_3_out, B2);
  not not_4 (not_4_out, B1);
  and and_3 (and_3_out, not_4_out, not_5_out);
  not not_5 (not_5_out, B0);
  and and_4 (and_4_out, B1, B0);
  not not_6 (not_6_out, B1);
  or or_1 (c, not_6_out, B0, B2);
  not not_7 (not_7_out, B2);
  and and_5 (and_5_out, not_7_out, not_8_out);
  not not_8 (not_8_out, B0);
  not not_9 (not_9_out, B2);
  and and_6 (and_6_out, not_9_out, B1);
  and and_7 (and_7_out, B1, not_10_out);
  not not_10 (not_10_out, B0);
  not not_11 (not_11_out, B1);
  and and_8 (and_8_out, B2, not_11_out, B0);
  not not_12 (not_12_out, B2);
  and and_9 (and_9_out, not_12_out, not_13_out);
  not not_13 (not_13_out, B0);
  and and_10 (and_10_out, B1, not_14_out);
  not not_14 (not_14_out, B0);
  not not_15 (not_15_out, B1);
  and and_11 (and_11_out, not_15_out, not_16_out);
  not not_16 (not_16_out, B0);
  and and_12 (and_12_out, B2, not_17_out);
  not not_17 (not_17_out, B1);
  and and_13 (and_13_out, B2, not_18_out);
  not not_18 (not_18_out, B0);
  not not_19 (not_19_out, B2);
  and and_14 (and_14_out, not_19_out, B1);
  and and_15 (and_15_out, B1, not_20_out);
  not not_20 (not_20_out, B0);
  and and_16 (and_16_out, B2, not_21_out);
  not not_21 (not_21_out, B1);
  or or_2 (a, and_1_out, B1, and_2_out, B3);
  or or_3 (b, not_3_out, and_3_out, and_4_out);
  or or_4 (d, and_5_out, and_6_out, and_7_out, and_8_out, B3);
  or or_5 (e, and_9_out, and_10_out);
  or or_6 (f, and_11_out, and_12_out, and_13_out, B3);
  or or_7 (g, and_14_out, and_15_out, and_16_out, B3);
endmodule

// Decod. 5 bits p/ display
module Decodificador_5_bits_p__display (
  input  [4:0] Entrada,
  input  Complemento_de_2,
  output out_3,
  output out_4,
  output out_5,
  output out_6,
  output out_7,
  output out_8,
  output out_9,
  output out_10,
  output out_11,
  output out_12,
  output out_13,
  output out_14,
  output out_15
);

  wire and_1_out, and_2_out, xnor_1_out;
  wire [4:0] adder_1_out, divider_1_out, divider_2_out, E, multiplexer_1_out, not_1_out;
  wire [4:4] divider_1_rem, divider_2_rem, divider_3_rem;

  not not_1 (not_1_out[0], Entrada[0]);
  not not_2 (not_1_out[1], Entrada[1]);
  not not_3 (not_1_out[2], Entrada[2]);
  not not_4 (not_1_out[3], Entrada[3]);
  not not_5 (not_1_out[4], Entrada[4]);
  Adder #(.width(5)) adder_1 (.a(not_1_out), .b(5'b00001), .out(adder_1_out));  // open: cin, cout
  Multiplexer #(.width(5), .enable("false")) multiplexer_1 (
    .in0(Entrada), .in1(adder_1_out), .out(multiplexer_1_out), .sel(Complemento_de_2));
  // Probe on {divider_1_rem[4], out_11, out_12, out_13, out_14}
  xnor xnor_1 (xnor_1_out, Entrada[4], Complemento_de_2);
  Divider #(.width(5)) divider_1 (
    .a(E), .b(5'b01010), .out(divider_1_out), .rem({divider_1_rem[4], out_11, out_12, out_13, out_14}));  // open: upper
  Multiplexer #(.width(5), .enable("false")) multiplexer_2 (
    .in0(Entrada), .in1(multiplexer_1_out), .out(E), .sel(xnor_1_out));
  and and_1 (and_1_out, xnor_1_out, Complemento_de_2);
  and and_2 (and_2_out, Complemento_de_2, Entrada[4]);
  Divider #(.width(5)) divider_2 (
    .a(divider_1_out), .b(5'b01010), .out(divider_2_out),
    .rem({divider_2_rem[4], out_7, out_8, out_9, out_10}));  // open: upper
  // Probe on {divider_2_rem[4], out_7, out_8, out_9, out_10}
  or or_1 (out_15, and_1_out, and_2_out);
  Divider #(.width(5)) divider_3 (
    .a(divider_2_out), .b(5'b01010), .rem({divider_3_rem[4], out_3, out_4, out_5, out_6}));  // open: out, upper
  // Probe on {divider_3_rem[4], out_3, out_4, out_5, out_6}

  // Other names for the same wires on the sheet: d0 = out_14; d1 = out_13; d2 = out_12; d3 = out_11; d4 = out_10;
  //   d5 = out_9; d6 = out_8; d7 = out_7; d8 = out_6; d9 = out_5; d10 = out_4; d11 = out_3; neg = out_15

  // Notes on the sheet:
  //   DISPLAY 1
  //   DISPLAY 2
  //   DISPLAY 3
  //   DISPLAY 3
  //   SINAL NEGATIVO
  //   DISPLAY 2
  //   DISPLAY 1
endmodule

// Decod. 10 bits p/ display
module Decodificador_10_bits_p__display (
  input  [9:0] Entrada,
  input  Complemento_de_2,
  output out_3,
  output out_4,
  output out_5,
  output out_6,
  output out_7,
  output out_8,
  output out_9,
  output out_10,
  output out_11,
  output out_12,
  output out_13,
  output out_14,
  output out_15
);

  wire and_1_out, and_2_out, and_3_out, not_11_out, not_12_out, not_14_out, xnor_1_out;
  wire [9:0] adder_1_out, divider_1_out, divider_2_out, E, multiplexer_1_out, not_1_out;
  wire [9:4] divider_1_rem, divider_2_rem, divider_3_rem;

  // Probe on Entrada
  not not_1 (not_1_out[0], Entrada[0]);
  not not_2 (not_1_out[1], Entrada[1]);
  not not_3 (not_1_out[2], Entrada[2]);
  not not_4 (not_1_out[3], Entrada[3]);
  not not_5 (not_1_out[4], Entrada[4]);
  not not_6 (not_1_out[5], Entrada[5]);
  not not_7 (not_1_out[6], Entrada[6]);
  not not_8 (not_1_out[7], Entrada[7]);
  not not_9 (not_1_out[8], Entrada[8]);
  not not_10 (not_1_out[9], Entrada[9]);
  not not_11 (not_11_out, Entrada[9]);
  not not_12 (not_12_out, Entrada[8]);
  and and_1 (and_1_out, not_11_out, not_12_out, not_14_out, Entrada[5]);
  // NOT_Gate not_13 has open pins: in=Entrada[7], out=open
  not not_14 (not_14_out, Entrada[6]);
  Adder #(.width(10)) adder_1 (.a(not_1_out), .b(10'h1), .out(adder_1_out));  // open: cin, cout
  // Probe on {divider_1_rem, out_11, out_12, out_13, out_14}
  Multiplexer #(.width(10), .enable("false")) multiplexer_1 (
    .in0(Entrada), .in1(adder_1_out), .out(multiplexer_1_out), .sel(Complemento_de_2));
  Divider #(.width(10)) divider_1 (
    .a(E), .b(10'ha), .out(divider_1_out), .rem({divider_1_rem, out_11, out_12, out_13, out_14}));  // open: upper
  Multiplexer #(.width(10), .enable("false")) multiplexer_2 (
    .in0(Entrada), .in1(multiplexer_1_out), .out(E), .sel(xnor_1_out));
  xnor xnor_1 (xnor_1_out, Complemento_de_2, Entrada[9]);
  Divider #(.width(10)) divider_2 (
    .a(divider_1_out), .b(10'ha), .out(divider_2_out), .rem({divider_2_rem, out_7, out_8, out_9, out_10}));  // open: upper
  // Probe on {divider_2_rem, out_7, out_8, out_9, out_10}
  and and_2 (and_2_out, xnor_1_out, Entrada[9]);
  and and_3 (and_3_out, Entrada[9], and_1_out);
  or or_1 (out_15, and_2_out, and_3_out);
  Divider #(.width(10)) divider_3 (
    .a(divider_2_out), .b(10'ha), .rem({divider_3_rem, out_3, out_4, out_5, out_6}));  // open: out, upper
  // Probe on {divider_3_rem, out_3, out_4, out_5, out_6}

  // Other names for the same wires on the sheet: d0 = out_14; d1 = out_13; d2 = out_12; d3 = out_11; d4 = out_10;
  //   d5 = out_9; d6 = out_8; d7 = out_7; d8 = out_6; d9 = out_5; d10 = out_4; d11 = out_3; neg = out_15

  // Notes on the sheet:
  //   DISPLAY 1
  //   Inverte todos os numeros
  //   DISPLAY 2
  //   soma 1
  //   DISPLAY 3
  //   Escolhe num negativo
  //   ou positivo
  //   DISPLAY 3
  //   SINAL NEGATIVO
  //   DISPLAY 2
  //   DISPLAY 1
endmodule

module Mostrar_5_bits (
  input  [4:0] Entrada,
  input  Sinal,
  output [4:0] Saida_sem_sinal,
  output [4:0] Saida_com_sinal
);

  Demultiplexer #(.width(5), .enable("false")) demultiplexer_1 (
    .out0(Saida_sem_sinal), .out1(Saida_com_sinal), .in(Entrada), .sel(Sinal));
endmodule

module Mostrar_10_bits (
  input  [9:0] Entrada,
  input  Sinal,
  output [9:0] Saida_sem_sinal,
  output [9:0] Saida_com_sinal
);

  Demultiplexer #(.width(10), .enable("false")) demultiplexer_1 (
    .out0(Saida_sem_sinal), .out1(Saida_com_sinal), .in(Entrada), .sel(Sinal));
endmodule
